// Logisim project nandy-modules.circ as structural Verilog
module main (
);

  wire aPCL_cout, undriven_6, undriven_7, undriven_8, undriven_9, undriven_10, undriven_11, undriven_12,
       undriven_13, undriven_14;
  wire [9:0] aPCH_q, aPCL_q, cInterrupt_q1, cInterrupt_q2, cSP___cJump_q1, cSP___cJump_q2, cSP___cJump_q3,
       mADDRH_q, mADDRL_q, mIMH_q, mIML_q, mLJH_q, mLJL_q, mOFFSH_q, mOFFSL_q, mSP_q, rPCH_q, rPCL_q,
       undriven, undriven_2, undriven_3, undriven_4, undriven_5, undriven_15;

  mod_mux mSP (.SEL(undriven_7), .A(undriven_2), .B(undriven), .Q(mSP_q));
  mod_muxes_const cSP___cJump (
    .SEL1(undriven_7), .A1(undriven_4), .const1({8{1'b1}}), .Q1(cSP___cJump_q1), .SEL2(undriven_13),
    .A2(undriven_5), .Q2(cSP___cJump_q2), .const2({8{1'b0}}), .SEL3(undriven_13), .A3(undriven_3),
    .Q3(cSP___cJump_q3), .const3(8'h1));
  mod_mux mOFFSL (.SEL(undriven_8), .A(cSP___cJump_q3), .B(undriven_5), .Q(mOFFSL_q));
  mod_mux mIML (.SEL(undriven_9), .A(rPCL_q), .B(mSP_q), .Q(mIML_q));
  mod_adder aPCL (.A(mIML_q), .B(mOFFSL_q), .Q(aPCL_q), .Cout(aPCL_cout));  // open: Cin
  mod_mux mLJL (.SEL(undriven_10), .A(aPCL_q), .B(undriven_2), .Q(mLJL_q));
  mod_muxes_const cInterrupt (
    .A1(mLJH_q), .const1(8'h7f), .Q1(cInterrupt_q1), .SEL2(undriven_14), .A2(mLJL_q), .Q2(cInterrupt_q2),
    .const2({8{1'b0}}), .SEL3(undriven_14));  // open: SEL1, A3, Q3, const3
  mod_register rPCL (.nRST(undriven_6), .WR(undriven_11), .D(cInterrupt_q2), .Q(rPCL_q));
  mod_mux mADDRL (.SEL(undriven_12), .A(aPCL_q), .B(rPCL_q), .Q(mADDRL_q));
  mod_mux mOFFSH (.SEL(undriven_8), .A(cSP___cJump_q2), .B(undriven_15), .Q(mOFFSH_q));
  mod_mux mIMH (.SEL(undriven_9), .A(rPCH_q), .B(cSP___cJump_q1), .Q(mIMH_q));
  mod_adder aPCH (.Cin(aPCL_cout), .A(mIMH_q), .B(mOFFSH_q), .Q(aPCH_q));  // open: Cout
  mod_mux mLJH (.SEL(undriven_10), .A(aPCH_q), .B(undriven_4), .Q(mLJH_q));
  mod_register rPCH (.nRST(undriven_6), .WR(undriven_11), .D(cInterrupt_q1), .Q(rPCH_q));
  mod_mux mADDRH (.SEL(undriven_12), .A(aPCH_q), .B(rPCH_q), .Q(mADDRH_q));

  // Notes on the sheet:
  //   SP
  //   DX
  //   LongOffs
  //   DY
  //   ShortOffs
  //   SEOffs
  //   ADDRH
  //   ADDRL
endmodule

module mod_register (
  input  nRST,
  input  WR,
  input  [9:0] D,
  output [9:0] Q
);

  wire not_1_out;

  not not_1 (not_1_out, nRST);
  slot_count slot_count_1 ();
  Register register_1 (.D(D[7:0]), .en(WR), .Q(Q[7:0]), .clk(D[9]), .clr(not_1_out));

  assign Q[9] = D[9];
endmodule

module mod_mux (
  input  SEL,
  input  [9:0] A,
  input  [9:0] B,
  output [9:0] Q
);

  slot_count slot_count_1 ();
  Multiplexer #(.width(9), .enable("false")) multiplexer_1 (.in0(A[8:0]), .in1(B[8:0]), .out(Q[8:0]), .sel(SEL));

  assign Q[9] = A[9];
endmodule

module mod_muxes_const (
  input  SEL1,
  input  [9:0] A1,
  input  [7:0] const1,
  input  SEL2,
  input  [9:0] A2,
  input  [7:0] const2,
  input  SEL3,
  input  [9:0] A3,
  input  [7:0] const3,
  output [9:0] Q1,
  output [9:0] Q2,
  output [9:0] Q3
);

  Multiplexer #(.width(8), .enable("false")) multiplexer_1 (.in0(A1[7:0]), .in1(const1), .out(Q1[7:0]), .sel(SEL1));
  slot_count slot_count_1 ();
  Multiplexer #(.width(8), .enable("false")) multiplexer_2 (.in0(A2[7:0]), .in1(const2), .out(Q2[7:0]), .sel(SEL2));
  Multiplexer #(.width(8), .enable("false")) multiplexer_3 (.in0(A3[7:0]), .in1(const3), .out(Q3[7:0]), .sel(SEL3));
  slot_count slot_count_2 ();

  assign Q1[9] = A1[9];
  assign Q2[9] = A2[9];
  assign Q3[9] = A3[9];
endmodule

module mod_adder (
  input  Cin,
  input  [9:0] A,
  input  [9:0] B,
  output [9:0] Q,
  output Cout
);

  Pull_Resistor pull_resistor_1 (.node(Cin));
  slot_count slot_count_1 ();
  Adder adder_1 (.a(A[7:0]), .b(B[7:0]), .out(Q[7:0]), .cin(Cin), .cout(Cout));
  slot_count slot_count_2 ();

  assign Q[9:8] = {A[9], Cout};
endmodule
