// Logisim project nandy-peripherals.circ as structural Verilog: 1 circuit, main circuit ps2_keyboard
module ps2_keyboard (
  input  Kb_Data,
  input  Core_IORead,
  output [7:0] CPU_IOBus,
  output CPU_IRQ
);

  wire and_1_out, and_2_out, Core_Clk_out, d_ff_1_qn, Kb_Clk_out, not_1_out, not_2_out, odd_parity_1_out,
       shift_register_1_q0, shift_register_1_q1, shift_register_1_q10;
  wire [7:0] shift_register_1_q2;

  Button Kb_Clk (.out(Kb_Clk_out));
  Button Core_Clk (.out(Core_Clk_out));
  not not_1 (not_1_out, and_1_out);
  Shift_Register #(.length(11)) shift_register_1 (
    .shift(not_1_out), .in(Kb_Data), .clk(Kb_Clk_out), .load(and_1_out), .d0(Kb_Data),
    .q0(shift_register_1_q0), .d1(1'b1), .q1(shift_register_1_q1), .d2(1'b1), .q2(shift_register_1_q2[0]),
    .d3(1'b1), .q3(shift_register_1_q2[1]), .d4(1'b1), .q4(shift_register_1_q2[2]), .d5(1'b1),
    .q5(shift_register_1_q2[3]), .d6(1'b1), .q6(shift_register_1_q2[4]), .d7(1'b1),
    .q7(shift_register_1_q2[5]), .d8(1'b1), .q8(shift_register_1_q2[6]), .d9(1'b1),
    .q9(shift_register_1_q2[7]), .d10(1'b1), .q10(shift_register_1_q10));  // open: out, clr
  D_Flip_Flop #(.trigger("falling")) d_ff_1 (
    .clk(Core_Clk_out), .D(and_1_out), .Qn(d_ff_1_qn));  // open: Q, preset, en, reset
  xor odd_parity_1 (odd_parity_1_out, shift_register_1_q1, shift_register_1_q2[0], shift_register_1_q2[1], shift_register_1_q2[2], shift_register_1_q2[3], shift_register_1_q2[4], shift_register_1_q2[5], shift_register_1_q2[6], shift_register_1_q2[7]);
  and and_1 (and_1_out, shift_register_1_q0, odd_parity_1_out, not_2_out);
  and and_2 (and_2_out, and_1_out, d_ff_1_qn);
  not not_2 (not_2_out, shift_register_1_q10);
  S_R_Flip_Flop #(.trigger("falling")) s_r_ff_1 (
    .S(and_2_out), .clk(Core_Clk_out), .R(Core_IORead), .Q(CPU_IRQ));  // open: Qn, preset, reset, en
  Hex_Digit_Display hex_digit_display_1 (.value(CPU_IOBus[7:4]));  // open: dp
  Register #(.trigger("high")) register_1 (
    .D(shift_register_1_q2), .en(and_2_out), .Q(CPU_IOBus), .clk(Core_Clk_out));  // open: clr
  Hex_Digit_Display hex_digit_display_2 (.value(CPU_IOBus[3:0]));  // open: dp
endmodule
